// Logisim project exercice4_Q7.circ as structural Verilog: 1 circuit, main circuit main
module main (
  output Q0,
  output Q1,
  output Q2
);

  wire and_1_out, and_2_out, and_3_out, and_4_out, clock_1_out, not_1_out, not_2_out, not_3_out;

  Clock clock_1 (.out(clock_1_out));
  J_K_Flip_Flop j_k_ff_1 (.J(1'b0), .K(1'b0), .clk(clock_1_out), .Q(Q0));  // open: Qn, preset, reset
  not not_1 (not_1_out, Q0);
  and and_1 (and_1_out, Q1, not_1_out);
  not not_2 (not_2_out, Q1);
  and and_2 (and_2_out, not_2_out, not_1_out);
  J_K_Flip_Flop j_k_ff_2 (.J(and_2_out), .K(and_1_out), .clk(clock_1_out), .Q(Q1));  // open: Qn, preset, reset
  and and_3 (and_3_out, not_3_out, and_2_out);
  and and_4 (and_4_out, Q2, and_2_out);
  not not_3 (not_3_out, Q2);
  J_K_Flip_Flop j_k_ff_3 (.J(and_3_out), .K(and_4_out), .clk(clock_1_out), .Q(Q2));  // open: Qn, preset, reset
endmodule
