// Logisim project exercice3.circ as structural Verilog: 1 circuit, main circuit main
module main (
  output Q0,
  output Q1,
  output Q2
);

  wire clock_1_out, not_1_out, xor_1_out;

  Clock clock_1 (.out(clock_1_out));
  D_Flip_Flop d_ff_1 (.D(1'b0), .clk(clock_1_out), .Q(Q0));  // open: Qn, preset, reset
  D_Flip_Flop d_ff_2 (.D(not_1_out), .clk(clock_1_out), .Q(Q1));  // open: Qn, preset, reset
  not not_1 (not_1_out, Q1);
  xor xor_1 (xor_1_out, Q1, Q2);
  D_Flip_Flop d_ff_3 (.D(xor_1_out), .clk(clock_1_out), .Q(Q2));  // open: Qn, preset, reset
endmodule
