// Logisim project exercice1.circ as structural Verilog
module exercice_1_Q2c (
  input  Ai,
  input  Bi,
  input  Ri_1,
  input  Ai2,
  input  Bi2,
  input  Ri_1_2,
  output Di,
  output Ri,
  output Di2,
  output Ri2
);

  wire and_1_out, and_2_out, demi_additionneur_1_out_3, demi_additionneur_1_out_4, demi_soustracteur_1_out_4,
       not_1_out, not_2_out, xor_1_out;

  not not_1 (not_1_out, Ai);
  xor xor_1 (xor_1_out, Ai, Bi);
  and and_1 (and_1_out, not_1_out, Bi);
  demi_additionneur demi_additionneur_1 (
    .in_1(Bi2), .in_2(Ri_1_2), .out_3(demi_additionneur_1_out_3), .out_4(demi_additionneur_1_out_4));
  not not_2 (not_2_out, xor_1_out);
  and and_2 (and_2_out, not_2_out, Ri_1);
  xor xor_2 (Di, xor_1_out, Ri_1);
  or or_1 (Ri, and_1_out, and_2_out);
  demi_soustracteur demi_soustracteur_1 (
    .in_1(Ai2), .in_2(demi_additionneur_1_out_3), .out_3(Di2), .out_4(demi_soustracteur_1_out_4));
  or or_2 (Ri2, demi_soustracteur_1_out_4, demi_additionneur_1_out_4);
endmodule

module exercice_1_Q2d (
  input  Ai,
  input  Bi,
  input  Ri_1,
  output Di,
  output Ri
);

  wire demi_soustracteur_1_out_3, demi_soustracteur_1_out_4, demi_soustracteur_2_out_4;

  demi_soustracteur demi_soustracteur_1 (
    .in_1(Ai), .in_2(Bi), .out_3(demi_soustracteur_1_out_3), .out_4(demi_soustracteur_1_out_4));
  demi_soustracteur demi_soustracteur_2 (
    .in_1(demi_soustracteur_1_out_3), .in_2(Ri_1), .out_3(Di), .out_4(demi_soustracteur_2_out_4));
  or or_1 (Ri, demi_soustracteur_1_out_4, demi_soustracteur_2_out_4);
endmodule

module demi_soustracteur (
  input  in_1,
  input  in_2,
  output out_3,
  output out_4
);

  wire not_1_out;

  not not_1 (not_1_out, in_1);
  xor xor_1 (out_3, in_1, in_2);
  and and_1 (out_4, in_2, not_1_out);
endmodule

module demi_additionneur (
  input  in_1,
  input  in_2,
  output out_3,
  output out_4
);

  xor xor_1 (out_3, in_1, in_2);
  and and_1 (out_4, in_1, in_2);
endmodule
