// Logisim project exercice3.circ as structural Verilog
module mux_4_vers_1 (
  input  E0,
  input  E1,
  input  E2,
  input  in_4,
  input  E3,
  input  [1:0] a0_a1,
  output S
);

  Multiplexer #(.enable("true"), .select(2)) multiplexer_1 (
    .in0(E0), .in1(E1), .in2(E2), .in3(E3), .out(S), .sel(a0_a1), .en(in_4));
endmodule

module mux_8_vers_1 (
  input  E0,
  input  E1,
  input  E2,
  input  E3,
  input  E4,
  input  E5,
  input  E6,
  input  a2,
  input  E7,
  input  [1:0] a0_a1,
  output S
);

  wire multiplexer_1_out, multiplexer_2_out, not_1_out;

  Multiplexer #(.enable("true"), .select(2)) multiplexer_1 (
    .in0(E0), .in1(E1), .in2(E2), .in3(E3), .out(multiplexer_1_out), .sel(a0_a1), .en(a2));
  Multiplexer #(.enable("true"), .select(2)) multiplexer_2 (
    .in0(E4), .in1(E5), .in2(E6), .in3(E7), .out(multiplexer_2_out), .sel(a0_a1), .en(not_1_out));
  not not_1 (not_1_out, a2);
  or or_1 (S, multiplexer_1_out, multiplexer_2_out);
endmodule
