// Logisim project exercice4.circ as structural Verilog
module demultiplexeur_1_vers_8 (
  input  E,
  input  [2:0] in_2,
  output S1,
  output S2,
  output f1,
  output S3,
  output S4,
  output S5,
  output S6,
  output S7,
  output S8,
  output f2
);

  Demultiplexer #(.select(3)) demultiplexer_1 (
    .out0(S1), .out1(S2), .out2(S3), .out3(S4), .out4(S5), .out5(S6), .out6(S7), .out7(S8), .in(E), .sel(in_2));
  or or_1 (f1, S1, S2, S5, S7);
  or or_2 (f2, S3, S7);
endmodule
