// Logisim project exercice6.circ as structural Verilog
module distributeur (
  input  e,
  input  c,
  input  m,
  input  p,
  output Ae,
  output Ac,
  output Am,
  output Ap
);

  wire and_1_out, and_2_out, not_1_out, not_2_out, not_3_out, xor_1_out;

  not not_1 (not_1_out, c);
  not not_2 (not_2_out, m);
  xor xor_1 (xor_1_out, m, c);
  not not_3 (not_3_out, xor_1_out);
  and and_1 (and_1_out, not_2_out, not_1_out, e);
  and and_2 (and_2_out, p, xor_1_out);
  and and_3 (Ac, p, c, not_2_out);
  and and_4 (Am, p, m, not_1_out);
  and and_5 (Ap, p, not_3_out);
  or or_1 (Ae, and_1_out, and_2_out);
endmodule
