// Logisim project exercice2.circ as structural Verilog
module compteur_asynchrone_modulo_16 (
  output out_1,
  output out_2,
  output out_3,
  output out_4
);

  wire clock_1_out;

  Clock clock_1 (.out(clock_1_out));
  J_K_Flip_Flop #(.trigger("falling")) j_k_ff_1 (
    .J(1'b1), .K(1'b1), .clk(clock_1_out), .Q(out_1));  // open: Qn, preset, reset
  J_K_Flip_Flop #(.trigger("falling")) j_k_ff_2 (
    .J(1'b1), .K(1'b1), .clk(out_1), .Q(out_2));  // open: Qn, preset, reset
  J_K_Flip_Flop #(.trigger("falling")) j_k_ff_3 (
    .J(1'b1), .K(1'b1), .clk(out_2), .Q(out_3));  // open: Qn, preset, reset
  J_K_Flip_Flop #(.trigger("falling")) j_k_ff_4 (
    .J(1'b1), .K(1'b1), .clk(out_3), .Q(out_4));  // open: Qn, preset, reset
endmodule

module comteur_asynchrone_modulo_10 (
  output Q0,
  output Q1,
  output Q2,
  output Q3
);

  wire clock_1_out, nand_1_out, not_1_out;

  J_K_Flip_Flop #(.trigger("falling")) j_k_ff_1 (
    .J(1'b1), .K(1'b1), .clk(clock_1_out), .Q(Q0), .reset(not_1_out));  // open: Qn, preset
  Clock clock_1 (.out(clock_1_out));
  J_K_Flip_Flop #(.trigger("falling")) j_k_ff_2 (
    .J(1'b1), .K(1'b1), .clk(Q0), .Q(Q1), .reset(not_1_out));  // open: Qn, preset
  J_K_Flip_Flop #(.trigger("falling")) j_k_ff_3 (
    .J(1'b1), .K(1'b1), .clk(Q1), .Q(Q2), .reset(not_1_out));  // open: Qn, preset
  J_K_Flip_Flop #(.trigger("falling")) j_k_ff_4 (
    .J(1'b1), .K(1'b1), .clk(Q2), .Q(Q3), .reset(not_1_out));  // open: Qn, preset
  nand nand_1 (nand_1_out, Q3, Q1);
  not not_1 (not_1_out, nand_1_out);
endmodule
