// Logisim project exercice3.circ as structural Verilog
module compteu_synchrone_modulo_16 (
  output Q3,
  output Q0,
  output Q1,
  output Q2
);

  wire and_1_out, and_2_out, clock_1_out;

  Clock clock_1 (.out(clock_1_out));
  J_K_Flip_Flop #(.trigger("falling")) j_k_ff_1 (
    .J(1'b1), .K(1'b1), .clk(clock_1_out), .Q(Q0));  // open: Qn, preset, reset
  J_K_Flip_Flop #(.trigger("falling")) j_k_ff_2 (.J(Q0), .K(Q0), .clk(clock_1_out), .Q(Q1));  // open: Qn, preset, reset
  and and_1 (and_1_out, Q1, Q0);
  J_K_Flip_Flop #(.trigger("falling")) j_k_ff_3 (
    .J(and_1_out), .K(and_1_out), .clk(clock_1_out), .Q(Q2));  // open: Qn, preset, reset
  and and_2 (and_2_out, and_1_out, Q2);
  J_K_Flip_Flop #(.trigger("falling")) j_k_ff_4 (
    .J(and_2_out), .K(and_2_out), .clk(clock_1_out), .Q(Q3));  // open: Qn, preset, reset
endmodule

module compteur_synchrone_modulo10 (
  output Q0,
  output Q1,
  output Q2,
  output Q3
);

  wire and_1_out, and_2_out, and_3_out, clock_1_out, j_k_ff_4_qn;

  Clock clock_1 (.out(clock_1_out));
  J_K_Flip_Flop #(.trigger("falling")) j_k_ff_1 (
    .J(1'b1), .K(1'b1), .clk(clock_1_out), .Q(Q0));  // open: Qn, preset, reset
  and and_1 (and_1_out, Q0, Q1);
  and and_2 (and_2_out, Q0, j_k_ff_4_qn);
  J_K_Flip_Flop #(.trigger("falling")) j_k_ff_2 (
    .J(and_2_out), .K(Q0), .clk(clock_1_out), .Q(Q1));  // open: Qn, preset, reset
  J_K_Flip_Flop #(.trigger("falling")) j_k_ff_3 (
    .J(and_1_out), .K(and_1_out), .clk(clock_1_out), .Q(Q2));  // open: Qn, preset, reset
  and and_3 (and_3_out, Q1, Q0, Q2);
  J_K_Flip_Flop #(.trigger("falling")) j_k_ff_4 (
    .J(and_3_out), .K(Q0), .clk(clock_1_out), .Q(Q3), .Qn(j_k_ff_4_qn));  // open: preset, reset
endmodule
